# Fritzing sketch display_7seg (saved by Fritzing 1.0.4)
breadboards: 1

parts:
  Part1 = Arduino Uno (Rev3)
  7_Segment1 = 7 Segment Display
  R1 = Resistor [tolerance=±5% power=0.25W resistance=220 package=THT]
  R2 = Resistor [tolerance=±5% power=0.25W resistance=220 package=THT]
  R3 = Resistor [tolerance=±5% power=0.25W resistance=220 package=THT]
  R4 = Resistor [tolerance=±5% power=0.25W resistance=220 package=THT]
  R5 = Resistor [tolerance=±5% power=0.25W resistance=220 package=THT]
  R6 = Resistor [tolerance=±5% power=0.25W resistance=220 package=THT]
  R7 = Resistor [tolerance=±5% power=0.25W resistance=220 package=THT]
  R8 = Resistor [tolerance=±5% power=0.25W resistance=220 package=THT]
  R9 = Resistor [tolerance=±5% power=0.25W resistance=10000 package=THT]
  S1 = Pushbutton [package="[THT]"]

nets:
  N1: Part1.D8, R5.Pin_0
  N2: Part1.D9_PWM, R6.Pin_0
  N3: Part1.D10_PWM/SS, R7.Pin_1
  N4: Part1.D11_PWM/MOSI, R8.Pin_1
  N5: Part1.D3_PWM, R9.Pin_1, S1.Pin_3, S1.Pin_4
  N6: Part1.D4, R1.Pin_1
  N7: Part1.D5_PWM, R2.Pin_1
  N8: Part1.D6_PWM, R4.Pin_0
  N9: Part1.D7, R3.Pin_0
  N10: Part1.5V, S1.Pin_1, S1.Pin_2
  N11: Part1.GND, 7_Segment1.common_cathode#3, R9.Pin_0
  N12: 7_Segment1.Segment_A#1, R8.Pin_0
  N13: 7_Segment1.Segment_F, R7.Pin_0
  N14: 7_Segment1.Segment_E, R6.Pin_1
  N15: 7_Segment1.Segment_D, R5.Pin_1
  N16: 7_Segment1.Segment_DP, R3.Pin_1
  N17: 7_Segment1.Segment_C, R4.Pin_1
  N18: 7_Segment1.Segment_B, R2.Pin_0
  N19: 7_Segment1.Segment_A#10, R1.Pin_0
