# Fritzing sketch distance_sensor_led_ramp (saved by Fritzing 1.0.4)
breadboards: 1

parts:
  Part1 = Arduino Uno (Rev3)
  LED1 = LED - 3mm [color="Red (633nm)" current=30mA package="3 mm [THT]"]
  R1 = Resistor [tolerance=±5% power=0.25W resistance=1000 package=THT]
  HC-SR04_Sensor_1 = HC-SR04 Ultrasonic Distance Sensor

nets:
  N1: Part1.D9_PWM, HC-SR04_Sensor_1.ECHO
  N2: Part1.D10_PWM/SS, HC-SR04_Sensor_1.TRIG
  N3: Part1.D3_PWM, LED1.cathode, LED1.anode, R1.Pin_0
  5V: Part1.5V, HC-SR04_Sensor_1.VCC
  GND: Part1.GND, R1.Pin_1, HC-SR04_Sensor_1.GND
